# Fritzing sketch FastLED_Demo1 (saved by Fritzing 0.9.3b)
breadboards: 1

parts:
  Part1 = Arduino Uno (Rev3)
  Power_plug1 = Power plug
  C1 = Electrolytic Capacitor [capacitance=1mF voltage=50V package="100 mil [THT, electrolytic]"]
  U1 = mystery part, 3 pins [chip_label=RGBs]

nets:
  N1: Part1.D3_PWM, U1.pin2
  GND: Part1.GND, Power_plug1.GND, C1.+, U1.pin3
  N2: Power_plug1.VCC, C1.-, U1.pin1
